# Fritzing sketch Sketch (saved by Fritzing 0.9.3b)

parts:
  YF-S201_Flow_Meter2 = YF-S201 Water Flow Meter
  U1 = NodeMCU V1.0

nets:
  N1: YF-S201_Flow_Meter2.SIG, U1.D3
  GND: YF-S201_Flow_Meter2.GND, U1.GND
  VCC: YF-S201_Flow_Meter2.VCC, U1.3V3

notes:
  Red wire : +5V
  Black wire : GND
  Yellow wire : PWM output

custom parts:
  YF-S201 Water Flow Meter: The YF-S201 Flow Meter. The input voltage is 5V to 24V (DC).
  NodeMCU V1.0: ESP8266 based NodeMCU
